# Fritzing sketch smart vacuum (saved by Fritzing 0.9.3b)

parts:
  MCU1 = Raspberry Pi Zero
  Part1 = Arduino Nano (Rev3.0)
  IC1 = Rasberry Pi NIOR Camera [chip_label=IC package="DIP (Dual Inline) [THT]"]  # not connected
  U2 = RELAY [package=relay-g5q]
  U3 = RELAY [package=relay-g5q]
  U4 = RELAY [package=relay-g5q]
  U5 = RELAY [package=relay-g5q]
  U6 = RELAY [package=relay-g5q]
  U8 = RELAY [package=relay-g5q]
  M1 = DC Motor  # not connected
  M2 = DC Motor  # not connected
  M3 = DC Motor
  VCC1 = Battery
  VCC2 = Battery  # not connected
  VCC3 = Battery  # not connected
  HC-SR04_Sensor_1 = HC-SR04 Ultrasonic Distance Sensor
  HC-SR04_Sensor_2 = HC-SR04 Ultrasonic Distance Sensor
  HC-SR04_Sensor_3 = HC-SR04 Ultrasonic Distance Sensor

nets:
  N1: MCU1.pin_36, Part1.D8
  N2: MCU1.pin_37, Part1.D11/MOSI
  N3: MCU1.pin_38, Part1.D9
  N4: MCU1.pin_40, Part1.D10
  N5: Part1.D2, U8.NO
  N6: Part1.D3, U6.NO
  N7: Part1.D4, U5.NO
  N8: Part1.D5, U4.NO
  N9: Part1.D6, U3.NO
  N10: Part1.D7, U2.NO
  N11: Part1.A7, HC-SR04_Sensor_1.TRIG
  N12: Part1.A6, HC-SR04_Sensor_1.ECHO
  N13: Part1.A5, HC-SR04_Sensor_2.TRIG
  N14: Part1.A4, HC-SR04_Sensor_2.ECHO
  N15: Part1.A3, HC-SR04_Sensor_3.TRIG
  N16: Part1.A2, HC-SR04_Sensor_3.ECHO
  N17: U4.COIL2, U5.COIL2
  N18: U4.NC, U4.COIL1, U5.NC, U5.COIL1, U6.NC, U6.COIL1, U8.NC, U8.COIL1, M3.pin_2, VCC1.-
  N19: U6.COIL2, VCC1.+
  VCC: HC-SR04_Sensor_1.VCC, HC-SR04_Sensor_2.VCC
  GND: HC-SR04_Sensor_1.GND, HC-SR04_Sensor_2.GND, HC-SR04_Sensor_3.GND

custom parts:
  Rasberry Pi NIOR Camera: Camera
